// Logisim project alu.circ as structural Verilog: 1 circuit, main circuit main
module main (
  input  [31:0] X,
  input  [31:0] Y,
  input  [3:0] Switch,
  input  [31:0] in_4,
  output Signed_Overflow,
  output Equal,
  output [31:0] Result
);

  wire a_detect, a_ov, s_detect, s_ov, sltbit, sltbitu;
  wire [3:0] Switch_t;
  wire [4:0] sinput;
  wire [31:0] add, addu, \and , \or , sll, slt, sltu, sra, srl, sub, subu;

  Shifter #(.width(32)) shifter_1 (.in(Y), .\dist (sinput), .out(sll));
  Shifter #(.width(32), .shift("lr")) shifter_2 (.in(Y), .\dist (sinput), .out(srl));
  Shifter #(.width(32), .shift("ar")) shifter_3 (.in(Y), .\dist (sinput), .out(sra));
  assign \or  = X | Y;  // OR_Gate or_1, 32 bits wide
  assign \and  = X & Y;  // AND_Gate and_1, 32 bits wide
  Bit_Extender #(.in_width(32), .out_width(5)) bit_extender_1 (.in(X), .out(sinput));
  Adder #(.width(32)) adder_1 (.a(X), .b(Y), .out(add), .cout(a_detect));  // open: cin
  Adder #(.width(32)) adder_2 (.a(X), .b(Y), .out(addu));  // open: cin, cout
  Subtractor #(.width(32)) subtractor_1 (.a(X), .b(Y), .out(sub), .bout(s_detect));  // open: bin
  Comparator #(.width(4)) comparator_1 (.a(Switch_t), .b(4'b0101), .eq(a_ov));  // open: gt, lt
  Comparator #(.width(4)) comparator_2 (.a(Switch_t), .b(4'b0111), .eq(s_ov));  // open: gt, lt
  Subtractor #(.width(32)) subtractor_2 (.a(X), .b(Y), .out(subu));  // open: bin, bout
  Comparator #(.width(32)) comparator_3 (.a(X), .b(Y), .eq(Equal));  // open: gt, lt
  Comparator #(.width(32)) comparator_4 (.a(X), .b(Y), .lt(sltbit));  // open: gt, eq
  assign slt = {{31{1'b0}}, sltbit};  // Bit_Extender bit_extender_2
  Comparator #(.width(32), .mode("unsigned")) comparator_5 (.a(X), .b(Y), .lt(sltbitu));  // open: gt, eq
  assign sltu = {{31{1'b0}}, sltbitu};  // Bit_Extender bit_extender_3
  and and_2 (Signed_Overflow, a_detect, a_ov);
  and and_3 (Signed_Overflow, s_detect, s_ov);
  Multiplexer #(.select(4), .width(32)) multiplexer_1 (
    .in0(sll), .in1(srl), .in2(sra), .in3(in_4), .in4(in_4), .in5(add), .in6(addu), .in7(sub), .in8(subu),
    .in9(\and ), .in10(\or ), .in11(slt), .in12(sltu), .in13(in_4), .in14(in_4), .in15(in_4), .out(Result),
    .sel(Switch_t));  // open: en

  // Other names for the same wires on the sheet: overflow = Signed_Overflow; S[3:0] = Switch; zero[31:0] = in_4

  // Notes on the sheet:
  //   INPUTS to your circuit
  //   DON'T CHANGE THE LOCATIONS OF THE INPUTS AND OUTPUTS!
  //   OUTPUTS from your circuit
endmodule
